// Logisim project CPU-DESIGN.circ as structural Verilog: 18 circuits, main circuit main
module main (
);


  // Notes on the sheet:
  //   Mohammad H. Mansour 120180606 
  //   Ahmed B. Abu Sharar 120180436 
  //   Osama R. Rashid 120181499
endmodule

module CU (
  input  [5:0] OP_CODE,
  output RegDst,
  output ALUSrc,
  output MemtoReg,
  output RegWrite,
  output MemRead,
  output MemWrite,
  output Branch,
  output [2:0] ALUOp_2_1_0,
  output Jump,
  output EX_1,
  output EX_0
);

  wire addiu_out, ori_out, slti_out, xori_out;

  and slti (slti_out, ~OP_CODE[5], ~OP_CODE[4], OP_CODE[3], ~OP_CODE[2], OP_CODE[1], ~OP_CODE[0]);  // AND_Gate
  and xori (xori_out, ~OP_CODE[5], ~OP_CODE[4], OP_CODE[3], OP_CODE[2], OP_CODE[1], ~OP_CODE[0]);  // AND_Gate
  and andi (EX_1, ~OP_CODE[5], ~OP_CODE[4], OP_CODE[3], OP_CODE[2], ~OP_CODE[1], ~OP_CODE[0]);  // AND_Gate
  and ori (ori_out, ~OP_CODE[5], ~OP_CODE[4], OP_CODE[3], OP_CODE[2], ~OP_CODE[1], OP_CODE[0]);  // AND_Gate
  and addiu (addiu_out, ~OP_CODE[5], ~OP_CODE[4], OP_CODE[3], ~OP_CODE[2], ~OP_CODE[1], OP_CODE[0]);  // AND_Gate
  and j (Jump, ~OP_CODE[5], ~OP_CODE[4], ~OP_CODE[3], ~OP_CODE[2], OP_CODE[1], ~OP_CODE[0]);  // AND_Gate
  and beq (Branch, ~OP_CODE[5], ~OP_CODE[4], ~OP_CODE[3], OP_CODE[2], ~OP_CODE[1], ~OP_CODE[0]);  // AND_Gate
  and sw (MemWrite, OP_CODE[5], ~OP_CODE[4], OP_CODE[3], ~OP_CODE[2], OP_CODE[1], OP_CODE[0]);  // AND_Gate
  and lw (MemRead, OP_CODE[5], ~OP_CODE[4], ~OP_CODE[3], ~OP_CODE[2], OP_CODE[1], OP_CODE[0]);  // AND_Gate
  or or_1 (ALUOp_2_1_0[0], Branch, addiu_out, xori_out, EX_1);
  or or_2 (ALUOp_2_1_0[1], ori_out, EX_1, addiu_out, slti_out);
  or or_3 (ALUOp_2_1_0[2], RegDst, xori_out, slti_out, addiu_out);
  and r_type (RegDst, ~OP_CODE[5], ~OP_CODE[4], ~OP_CODE[3], ~OP_CODE[2], ~OP_CODE[1], ~OP_CODE[0]);  // AND_Gate
  or or_4 (ALUSrc, slti_out, MemRead, addiu_out, MemWrite);
  or or_5 (RegWrite, xori_out, ori_out, RegDst, addiu_out, MemRead, EX_1, slti_out);
  or or_6 (EX_0, ori_out, xori_out);

  assign MemtoReg = MemRead;

  // Notes on the sheet:
  //   000          lw / sw
  //   001          beq
  //   010          ori        
  //   011          andi     
  //   100           r-type 
  //   101           xori
  //   110           slti
  //   111           addi
endmodule

module ALU_Control (
  input  [5:0] funct,
  input  [2:0] ALUOp,
  output [3:0] ALU_Cinput
);

  wire add_out, addi_out, beq_out, lw_out, nor_out, or_4_out, ori_out, slt_out, slti_out, sub_out, sw_out,
       xor_out, xori_out;

  and \nor  (nor_out, ALUOp[2], ~ALUOp[1], ~ALUOp[0], funct[5], ~funct[4], ~funct[3], funct[2], funct[1], funct[0]);  // AND_Gate
  and xori (xori_out, ALUOp[2], ~ALUOp[1], ALUOp[0]);  // AND_Gate
  and slti (slti_out, ALUOp[2], ALUOp[1], ~ALUOp[0]);  // AND_Gate
  and addi (addi_out, ALUOp[2], ALUOp[1], ALUOp[0]);
  // AND_Gate andi has open pins: in0=ALUOp[2], in1=ALUOp[1], in2=ALUOp[0], out=open
  and ori (ori_out, ~ALUOp[2], ALUOp[1], ~ALUOp[0]);  // AND_Gate
  and beq (beq_out, ~ALUOp[2], ~ALUOp[1], ALUOp[0]);  // AND_Gate
  and sw (sw_out, ~ALUOp[2], ~ALUOp[1], ~ALUOp[0]);  // AND_Gate
  or or_1 (ALU_Cinput[3], slt_out, beq_out, sub_out, slti_out);
  and lw (lw_out, ~ALUOp[2], ~ALUOp[1], ~ALUOp[0]);  // AND_Gate
  or or_2 (ALU_Cinput[2], xori_out, nor_out, xor_out);
  or or_3 (ALU_Cinput[1], addi_out, slt_out, slti_out, beq_out, sub_out, sw_out, lw_out, add_out);
  and slt (slt_out, ALUOp[2], ~ALUOp[1], ~ALUOp[0], funct[5], ~funct[4], funct[3], ~funct[2], funct[1], ~funct[0]);  // AND_Gate
  and \xor  (xor_out, ALUOp[2], ~ALUOp[1], ~ALUOp[0], funct[5], ~funct[4], ~funct[3], funct[2], funct[1], ~funct[0]);  // AND_Gate
  and or_4 (or_4_out, ALUOp[2], ~ALUOp[1], ~ALUOp[0], funct[5], ~funct[4], ~funct[3], funct[2], ~funct[1], funct[0]);  // AND_Gate
  // AND_Gate and has open pins: in0=ALUOp[2], in1=ALUOp[1], in2=ALUOp[0], in3=funct[5], in4=funct[4], in5=funct[3], in6=funct[2], in7=funct[1], in8=funct[0], out=open
  or or_5 (ALU_Cinput[0], slti_out, slt_out, nor_out, ori_out, or_4_out);
  and sub (sub_out, ALUOp[2], ~ALUOp[1], ~ALUOp[0], funct[5], ~funct[4], ~funct[3], ~funct[2], funct[1], funct[0]);  // AND_Gate
  and add (add_out, ALUOp[2], ~ALUOp[1], ~ALUOp[0], funct[5], ~funct[4], ~funct[3], ~funct[2], ~funct[1], funct[0]);  // AND_Gate

  // Notes on the sheet:
  //   0010   addu
  //   1010   subu
  //   0000   and
  //   0001   or
  //   0100   xor
  //   1011   slt
  //   1010   beq
  //   0001   ori
  //   0000   andi
  //   1011   slti
  //   0100   xori
  //   0010   lw / sw
  //   0010   addiu
endmodule

module ALU (
  input  c_in,
  input  A,
  input  B,
  input  less,
  input  [3:0] ALU_Cinput,
  output ZERO,
  output \output ,
  output c_out
);

  wire adder_1_out, and_1_out, multiplexer_1_out, not_1_out, not_2_out, or_1_out, xor_1_out;

  not not_1 (not_1_out, B);
  Multiplexer multiplexer_1 (.in0(B), .in1(not_1_out), .out(multiplexer_1_out), .sel(ALU_Cinput[3]));  // open: en
  and and_1 (and_1_out, A, multiplexer_1_out);
  or or_1 (or_1_out, A, multiplexer_1_out);
  Adder #(.width(1)) adder_1 (.a(A), .b(multiplexer_1_out), .out(adder_1_out), .cin(c_in), .cout(c_out));
  xor xor_1 (xor_1_out, A, multiplexer_1_out);
  not not_2 (not_2_out, or_1_out);
  not not_3 (ZERO, \output );
  Multiplexer #(.select(3)) multiplexer_2 (
    .in0(and_1_out), .in1(or_1_out), .in2(adder_1_out), .in3(less), .in4(xor_1_out), .in5(not_2_out),
    .in6(1'b0), .in7(1'b0), .out(\output ), .sel(ALU_Cinput[2:0]));  // open: en
endmodule

module _32_bit_ALU (
  input  [3:0] ALU_Cinput,
  input  [31:0] A,
  input  [31:0] B,
  output zero,
  output [31:0] result
);

  wire alu_1_c_out, alu_1_zero, alu_2_c_out, alu_2_zero, alu_3_c_out, alu_3_zero, alu_4_c_out, alu_4_zero,
       alu_5_c_out, alu_5_zero, alu_6_c_out, alu_6_zero, alu_7_c_out, alu_7_zero, alu_8_c_out, alu_8_zero,
       alu_9_c_out, alu_9_zero, alu_10_c_out, alu_10_zero, alu_11_c_out, alu_11_zero, alu_12_c_out,
       alu_12_zero, alu_13_c_out, alu_13_zero, alu_14_c_out, alu_14_zero, alu_15_c_out, alu_15_zero,
       alu_16_c_out, alu_16_zero, alu_17_c_out, alu_17_zero, alu_18_c_out, alu_18_zero, alu_19_c_out,
       alu_19_zero, alu_20_c_out, alu_20_zero, alu_21_c_out, alu_21_zero, alu_22_c_out, alu_22_zero,
       alu_23_c_out, alu_23_zero, alu_24_c_out, alu_24_zero, alu_25_c_out, alu_25_zero, alu_26_c_out,
       alu_26_zero, alu_27_c_out, alu_27_zero, alu_28_c_out, alu_28_zero, alu_29_c_out, alu_29_zero,
       alu_30_c_out, alu_30_zero, alu_31_c_out, alu_31_zero, alu_32_c_out, alu_32_zero, not_1_out;

  ALU alu_1 (
    .A(A[0]), .B(B[0]), .ZERO(alu_1_zero), .\output (result[0]), .c_out(alu_1_c_out), .c_in(ALU_Cinput[3]),
    .ALU_Cinput(ALU_Cinput), .less(not_1_out));
  ALU alu_2 (
    .A(A[1]), .B(B[1]), .ZERO(alu_2_zero), .\output (result[1]), .c_out(alu_2_c_out), .c_in(alu_1_c_out),
    .ALU_Cinput(ALU_Cinput), .less(1'b0));
  ALU alu_3 (
    .A(A[2]), .B(B[2]), .ZERO(alu_3_zero), .\output (result[2]), .c_out(alu_3_c_out), .c_in(alu_2_c_out),
    .ALU_Cinput(ALU_Cinput), .less(1'b0));
  ALU alu_4 (
    .A(A[3]), .B(B[3]), .ZERO(alu_4_zero), .\output (result[3]), .c_out(alu_4_c_out), .c_in(alu_3_c_out),
    .ALU_Cinput(ALU_Cinput), .less(1'b0));
  ALU alu_5 (
    .A(A[4]), .B(B[4]), .ZERO(alu_5_zero), .\output (result[4]), .c_out(alu_5_c_out), .c_in(alu_4_c_out),
    .ALU_Cinput(ALU_Cinput), .less(1'b0));
  ALU alu_6 (
    .A(A[5]), .B(B[5]), .ZERO(alu_6_zero), .\output (result[5]), .c_out(alu_6_c_out), .c_in(alu_5_c_out),
    .ALU_Cinput(ALU_Cinput), .less(1'b0));
  ALU alu_7 (
    .A(A[6]), .B(B[6]), .ZERO(alu_7_zero), .\output (result[6]), .c_out(alu_7_c_out), .c_in(alu_6_c_out),
    .ALU_Cinput(ALU_Cinput), .less(1'b0));
  ALU alu_8 (
    .A(A[7]), .B(B[7]), .ZERO(alu_8_zero), .\output (result[7]), .c_out(alu_8_c_out), .c_in(alu_7_c_out),
    .ALU_Cinput(ALU_Cinput), .less(1'b0));
  ALU alu_9 (
    .A(A[8]), .B(B[8]), .ZERO(alu_9_zero), .\output (result[8]), .c_out(alu_9_c_out), .c_in(alu_8_c_out),
    .ALU_Cinput(ALU_Cinput), .less(1'b0));
  ALU alu_10 (
    .A(A[9]), .B(B[9]), .ZERO(alu_10_zero), .\output (result[9]), .c_out(alu_10_c_out), .c_in(alu_9_c_out),
    .ALU_Cinput(ALU_Cinput), .less(1'b0));
  ALU alu_11 (
    .A(A[10]), .B(B[10]), .ZERO(alu_11_zero), .\output (result[10]), .c_out(alu_11_c_out),
    .c_in(alu_10_c_out), .ALU_Cinput(ALU_Cinput), .less(1'b0));
  ALU alu_12 (
    .A(A[11]), .B(B[11]), .ZERO(alu_12_zero), .\output (result[11]), .c_out(alu_12_c_out),
    .c_in(alu_11_c_out), .ALU_Cinput(ALU_Cinput), .less(1'b0));
  ALU alu_13 (
    .A(A[12]), .B(B[12]), .ZERO(alu_13_zero), .\output (result[12]), .c_out(alu_13_c_out),
    .c_in(alu_12_c_out), .ALU_Cinput(ALU_Cinput), .less(1'b0));
  ALU alu_14 (
    .A(A[13]), .B(B[13]), .ZERO(alu_14_zero), .\output (result[13]), .c_out(alu_14_c_out),
    .c_in(alu_13_c_out), .ALU_Cinput(ALU_Cinput), .less(1'b0));
  ALU alu_15 (
    .A(A[14]), .B(B[14]), .ZERO(alu_15_zero), .\output (result[14]), .c_out(alu_15_c_out),
    .c_in(alu_14_c_out), .ALU_Cinput(ALU_Cinput), .less(1'b0));
  ALU alu_16 (
    .A(A[15]), .B(B[15]), .ZERO(alu_16_zero), .\output (result[15]), .c_out(alu_16_c_out),
    .c_in(alu_15_c_out), .ALU_Cinput(ALU_Cinput), .less(1'b0));
  ALU alu_17 (
    .A(A[16]), .B(B[16]), .ZERO(alu_17_zero), .\output (result[16]), .c_out(alu_17_c_out),
    .c_in(alu_16_c_out), .ALU_Cinput(ALU_Cinput), .less(1'b0));
  ALU alu_18 (
    .A(A[17]), .B(B[17]), .ZERO(alu_18_zero), .\output (result[17]), .c_out(alu_18_c_out),
    .c_in(alu_17_c_out), .ALU_Cinput(ALU_Cinput), .less(1'b0));
  ALU alu_19 (
    .A(A[18]), .B(B[18]), .ZERO(alu_19_zero), .\output (result[18]), .c_out(alu_19_c_out),
    .c_in(alu_18_c_out), .ALU_Cinput(ALU_Cinput), .less(1'b0));
  ALU alu_20 (
    .A(A[19]), .B(B[19]), .ZERO(alu_20_zero), .\output (result[19]), .c_out(alu_20_c_out),
    .c_in(alu_19_c_out), .ALU_Cinput(ALU_Cinput), .less(1'b0));
  ALU alu_21 (
    .A(A[20]), .B(B[20]), .ZERO(alu_21_zero), .\output (result[20]), .c_out(alu_21_c_out),
    .c_in(alu_20_c_out), .ALU_Cinput(ALU_Cinput), .less(1'b0));
  ALU alu_22 (
    .A(A[21]), .B(B[21]), .ZERO(alu_22_zero), .\output (result[21]), .c_out(alu_22_c_out),
    .c_in(alu_21_c_out), .ALU_Cinput(ALU_Cinput), .less(1'b0));
  ALU alu_23 (
    .A(A[22]), .B(B[22]), .ZERO(alu_23_zero), .\output (result[22]), .c_out(alu_23_c_out),
    .c_in(alu_22_c_out), .ALU_Cinput(ALU_Cinput), .less(1'b0));
  ALU alu_24 (
    .A(A[23]), .B(B[23]), .ZERO(alu_24_zero), .\output (result[23]), .c_out(alu_24_c_out),
    .c_in(alu_23_c_out), .ALU_Cinput(ALU_Cinput), .less(1'b0));
  ALU alu_25 (
    .A(A[24]), .B(B[24]), .ZERO(alu_25_zero), .\output (result[24]), .c_out(alu_25_c_out),
    .c_in(alu_24_c_out), .ALU_Cinput(ALU_Cinput), .less(1'b0));
  ALU alu_26 (
    .A(A[25]), .B(B[25]), .ZERO(alu_26_zero), .\output (result[25]), .c_out(alu_26_c_out),
    .c_in(alu_25_c_out), .ALU_Cinput(ALU_Cinput), .less(1'b0));
  ALU alu_27 (
    .A(A[26]), .B(B[26]), .ZERO(alu_27_zero), .\output (result[26]), .c_out(alu_27_c_out),
    .c_in(alu_26_c_out), .ALU_Cinput(ALU_Cinput), .less(1'b0));
  ALU alu_28 (
    .A(A[27]), .B(B[27]), .ZERO(alu_28_zero), .\output (result[27]), .c_out(alu_28_c_out),
    .c_in(alu_27_c_out), .ALU_Cinput(ALU_Cinput), .less(1'b0));
  ALU alu_29 (
    .A(A[28]), .B(B[28]), .ZERO(alu_29_zero), .\output (result[28]), .c_out(alu_29_c_out),
    .c_in(alu_28_c_out), .ALU_Cinput(ALU_Cinput), .less(1'b0));
  ALU alu_30 (
    .A(A[29]), .B(B[29]), .ZERO(alu_30_zero), .\output (result[29]), .c_out(alu_30_c_out),
    .c_in(alu_29_c_out), .ALU_Cinput(ALU_Cinput), .less(1'b0));
  ALU alu_31 (
    .A(A[30]), .B(B[30]), .ZERO(alu_31_zero), .\output (result[30]), .c_out(alu_31_c_out),
    .c_in(alu_30_c_out), .ALU_Cinput(ALU_Cinput), .less(1'b0));
  ALU alu_32 (
    .A(A[31]), .B(B[31]), .ZERO(alu_32_zero), .\output (result[31]), .c_out(alu_32_c_out),
    .c_in(alu_31_c_out), .ALU_Cinput(ALU_Cinput), .less(1'b0));
  not not_1 (not_1_out, alu_32_c_out);
  and and_1 (zero, alu_1_zero, alu_2_zero, alu_3_zero, alu_4_zero, alu_5_zero, alu_6_zero, alu_7_zero, alu_8_zero, alu_9_zero, alu_10_zero, alu_11_zero, alu_12_zero, alu_13_zero, alu_14_zero, alu_15_zero, alu_16_zero, alu_17_zero, alu_18_zero, alu_19_zero, alu_20_zero, alu_21_zero, alu_22_zero, alu_23_zero, alu_24_zero, alu_25_zero, alu_26_zero, alu_27_zero, alu_28_zero, alu_29_zero, alu_30_zero, alu_31_zero, alu_32_zero);
endmodule

module Sign_Extended (
  input  [15:0] in_1,
  output [31:0] out_2
);


  assign out_2 = {{17{in_1[15]}}, in_1[14:0]};
endmodule

module _0_Extended (
  input  [15:0] in_1,
  output [31:0] out_2
);


  assign out_2 = {{16{1'b0}}, in_1};
endmodule

module _1_Extended (
  input  [15:0] in_1,
  output [31:0] out_2
);


  assign out_2 = {{16{1'b1}}, in_1};
endmodule

module MultiPlixer (
  input  [31:0] _0,
  input  Select,
  input  [31:0] _1,
  output [31:0] out_4
);

  Multiplexer #(.width(32)) multiplexer_1 (.in0(_0), .in1(_1), .out(out_4), .sel(Select));  // open: en
endmodule

module Shifter (
  input  [31:0] in_1,
  output [31:0] out_2
);

  Shifter_part #(.width(32)) shifter_1 (.in(in_1), .\dist (5'b00010), .out(out_2));
endmodule

module CPU (
  input  POWER_BTN
);

  wire and_1_out, clock_1_out, cu_1_alusrc, cu_1_branch, cu_1_ex_0, cu_1_ex_1, cu_1_jump, cu_1_memread,
       cu_1_memtoreg, cu_1_memwrite, cu_1_regdst, cu_1_regwrite, n32_bit_alu_1_zero;
  wire [2:0] cu_1_aluop_2_1_0;
  wire [3:0] alu_control_1_alu_cinput;
  wire [4:0] address_splitter_1_dist_reg, address_splitter_1_reg_1, address_splitter_1_reg_2,
       mux_5_bit_1_out_4;
  wire [5:0] address_splitter_1_funct, address_splitter_1_op_code;
  wire [15:0] address_splitter_1_immed;
  wire [23:0] memwrite_spliter_1_out_2;
  wire [25:0] address_splitter_1_j_type;
  wire [31:0] adder_alushape_1_out_3, alu_adder_1_out_3, mipsprogramrom_1_p2, multiplixer_1_1_out_4,
       multiplixer_1_out_4, multiplixer_2_out_4, multiplixer_3_out_4, multiplixer_4_out_4,
       n0_extended_1_out_2, n1_extended_1_out_2, n32_bit_alu_1_result, ram_1_data, register_1_q,
       registerfile_1_p1, registerfile_1_p7, registerfile_1_p8, shifter_1_out_2,
       shifter_concater_1_jump_address, sign_extended_1_out_2;

  Clock clock_1 (.out(clock_1_out));
  Register #(.width(32)) register_1 (
    .D(multiplixer_4_out_4), .en(POWER_BTN), .Q(register_1_q), .clk(clock_1_out), .clr(1'b0));
  Adder_ALUShape adder_alushape_1 (.in_1(register_1_q), .in_2(32'h4), .out_3(adder_alushape_1_out_3));
  // MIPSProgramROM mipsprogramrom_1: pin names not known; wires that end beside it: register_1_q, mipsprogramrom_1_p2
  Address_Splitter address_splitter_1 (
    .in_1(mipsprogramrom_1_p2), .funct(address_splitter_1_funct), .dist_Reg(address_splitter_1_dist_reg),
    .Reg_2(address_splitter_1_reg_2), .Reg_1(address_splitter_1_reg_1), .OP_code(address_splitter_1_op_code),
    .immed(address_splitter_1_immed), .J_type(address_splitter_1_j_type));  // open: Shift_amount
  Shifter_Concater shifter_concater_1 (
    ._26(address_splitter_1_j_type), .PC_Adder(adder_alushape_1_out_3),
    .jump_address(shifter_concater_1_jump_address));
  MUX_5_bit mux_5_bit_1 (
    ._0(address_splitter_1_reg_2), ._1(address_splitter_1_dist_reg), .out_4(mux_5_bit_1_out_4),
    .Select(cu_1_regdst));
  CU cu_1 (
    .OP_CODE(address_splitter_1_op_code), .RegDst(cu_1_regdst), .ALUSrc(cu_1_alusrc),
    .MemtoReg(cu_1_memtoreg), .RegWrite(cu_1_regwrite), .MemRead(cu_1_memread), .MemWrite(cu_1_memwrite),
    .Branch(cu_1_branch), .ALUOp_2_1_0(cu_1_aluop_2_1_0), .Jump(cu_1_jump), .EX_1(cu_1_ex_1), .EX_0(cu_1_ex_0));
  Sign_Extended sign_extended_1 (.in_1(address_splitter_1_immed), .out_2(sign_extended_1_out_2));
  _0_Extended u_0_extended_1 (.in_1(address_splitter_1_immed), .out_2(n0_extended_1_out_2));
  _1_Extended u_1_extended_1 (.in_1(address_splitter_1_immed), .out_2(n1_extended_1_out_2));
  // RegisterFile registerfile_1: pin names not known; wires that end beside it: registerfile_1_p1, clock_1_out, cu_1_regwrite, mux_5_bit_1_out_4, address_splitter_1_reg_1, address_splitter_1_reg_2, registerfile_1_p7, registerfile_1_p8
  MultiPlixer multiplixer_1 (
    ._0(registerfile_1_p8), ._1(sign_extended_1_out_2), .out_4(multiplixer_1_out_4), .Select(cu_1_alusrc));
  MultiPlixer multiplixer_2 (
    ._0(multiplixer_1_out_4), ._1(n0_extended_1_out_2), .out_4(multiplixer_2_out_4), .Select(cu_1_ex_0));
  MultiPlixer multiplixer_3 (
    ._0(multiplixer_2_out_4), ._1(n1_extended_1_out_2), .out_4(multiplixer_3_out_4), .Select(cu_1_ex_1));
  Shifter shifter_1 (.in_1(sign_extended_1_out_2), .out_2(shifter_1_out_2));
  _32_bit_ALU u_32_bit_alu_1 (
    .ALU_Cinput(alu_control_1_alu_cinput), .A(registerfile_1_p7), .B(multiplixer_3_out_4),
    .zero(n32_bit_alu_1_zero), .result(n32_bit_alu_1_result));
  ALU_Control alu_control_1 (
    .funct(address_splitter_1_funct), .ALUOp(cu_1_aluop_2_1_0), .ALU_Cinput(alu_control_1_alu_cinput));
  ALU_Adder alu_adder_1 (.in_1(adder_alushape_1_out_3), .in_2(shifter_1_out_2), .out_3(alu_adder_1_out_3));
  MemWrite_Spliter memwrite_spliter_1 (.in_1(registerfile_1_p8), .out_2(memwrite_spliter_1_out_2));
  MultiPlixer_1 multiplixer_1_1 (
    ._0(adder_alushape_1_out_3), ._1(alu_adder_1_out_3), .out_4(multiplixer_1_1_out_4), .Select(and_1_out));
  and and_1 (and_1_out, cu_1_branch, n32_bit_alu_1_zero);
  MultiPlixer multiplixer_4 (
    ._0(multiplixer_1_1_out_4), ._1(shifter_concater_1_jump_address), .out_4(multiplixer_4_out_4),
    .Select(cu_1_jump));
  RAM #(.addrWidth(24), .dataWidth(32), .bus("separate")) ram_1 (
    .addr(memwrite_spliter_1_out_2), .din(n32_bit_alu_1_result), .data(ram_1_data), .str(cu_1_memwrite),
    .sel(1'b1), .clk(clock_1_out), .ld(cu_1_memread), .clr(1'b0));
  MultiPlixer multiplixer_5 (
    ._0(n32_bit_alu_1_result), ._1(ram_1_data), .out_4(registerfile_1_p1), .Select(cu_1_memtoreg));
endmodule

module Address_Splitter (
  input  [31:0] in_1,
  output [25:0] J_type,
  output [5:0] funct,
  output [4:0] Shift_amount,
  output [4:0] dist_Reg,
  output [4:0] Reg_2,
  output [4:0] Reg_1,
  output [5:0] OP_code,
  output [15:0] immed
);


  assign dist_Reg = in_1[15:11];
  assign funct = in_1[5:0];
  assign immed = in_1[15:0];
  assign J_type = in_1[25:0];
  assign OP_code = in_1[31:26];
  assign Reg_1 = in_1[25:21];
  assign Reg_2 = in_1[20:16];
  assign Shift_amount = in_1[10:6];
endmodule

module MUX_5_bit (
  input  [4:0] _0,
  input  Select,
  input  [4:0] _1,
  output [4:0] out_4
);

  Multiplexer #(.width(5)) multiplexer_1 (.in0(_0), .in1(_1), .out(out_4), .sel(Select));  // open: en
endmodule

module MemWrite_Spliter (
  input  [31:0] in_1,
  output [23:0] out_2
);


  assign out_2 = in_1[23:0];
endmodule

module MultiPlixer_1 (
  input  [31:0] _0,
  input  Select,
  input  [31:0] _1,
  output [31:0] out_4
);

  Multiplexer #(.width(32)) multiplexer_1 (.in0(_0), .in1(_1), .out(out_4), .sel(Select));  // open: en
endmodule

module ALU_Adder (
  input  [31:0] in_1,
  input  [31:0] in_2,
  output [31:0] out_3
);

  Adder #(.width(32)) adder_1 (.a(in_1), .b(in_2), .out(out_3), .cin(1'b0));  // open: cout
endmodule

module Adder_ALUShape (
  input  [31:0] in_1,
  input  [31:0] in_2,
  output [31:0] out_3
);

  Adder #(.width(32)) adder_1 (.a(in_1), .b(in_2), .out(out_3), .cin(1'b0));  // open: cout
endmodule

module Shifter_Concater (
  input  [25:0] _26,
  input  [31:0] PC_Adder,
  output [31:0] jump_address
);


  assign jump_address = {PC_Adder[31:28], _26, 2'b00};
endmodule
