// Logisim project lab3.circ as structural Verilog: 4 circuits, main circuit main
module main (
  input  [3:0] in_1,
  input  [1:0] SELECT,
  input  READ_WRITE,
  output out_4,
  output [2:0] out_5,
  output [3:0] out_6
);

  wire CLOCK_out;

  Clock CLOCK (.out(CLOCK_out));
  BC bc_1 (.INPUT(in_1[0]), .OUTPUT(out_4), .SELECT(1'b1), .READ_WRITE(READ_WRITE), .CLOCK(CLOCK_out));
  _4x3_BC u_4x3_bc_1 (
    .ENABLE(1'b1), .ADDRESS(SELECT), .READ_WRITE(READ_WRITE), .CLOCK(CLOCK_out), .INPUT(in_1[2:0]),
    .OUTPUT(out_5));
  _4x4_BC u_4x4_bc_1 (
    .ENABLE(1'b1), .ADDRESS(SELECT), .READ_WRITE(READ_WRITE), .CLOCK(CLOCK_out), .INPUT(in_1), .OUTPUT(out_6));
endmodule

module BC (
  input  SELECT,
  input  INPUT,
  input  READ_WRITE,
  input  CLOCK,
  output OUTPUT
);

  wire and_1_out, and_2_out, not_1_out, not_2_out, s_r_ff_1_q;

  not not_1 (not_1_out, INPUT);
  and and_1 (and_1_out, SELECT, not_2_out, not_1_out);
  and and_2 (and_2_out, SELECT, not_2_out, INPUT);
  not not_2 (not_2_out, READ_WRITE);
  S_R_Flip_Flop s_r_ff_1 (
    .S(and_2_out), .clk(CLOCK), .R(and_1_out), .Q(s_r_ff_1_q), .preset(1'b0), .reset(1'b0), .en(SELECT));  // open: Qn
  and and_3 (OUTPUT, SELECT, s_r_ff_1_q, READ_WRITE);
endmodule

module _4x3_BC (
  input  [2:0] INPUT,
  input  ENABLE,
  input  [1:0] ADDRESS,
  input  READ_WRITE,
  input  CLOCK,
  output [2:0] OUTPUT
);

  wire bc_1_output, bc_2_output, bc_3_output, bc_4_output, bc_5_output, bc_6_output, bc_7_output,
       bc_8_output, bc_9_output, bc_10_output, bc_11_output, bc_12_output, decoder_1_out0, decoder_1_out1,
       decoder_1_out2, decoder_1_out3;

  Decoder #(.select(2)) decoder_1 (
    .out0(decoder_1_out0), .out1(decoder_1_out1), .out2(decoder_1_out2), .out3(decoder_1_out3),
    .sel(ADDRESS), .en(ENABLE));
  BC bc_1 (.INPUT(INPUT[0]), .OUTPUT(bc_1_output), .SELECT(decoder_1_out0), .READ_WRITE(READ_WRITE), .CLOCK(CLOCK));
  BC bc_2 (.INPUT(INPUT[0]), .OUTPUT(bc_2_output), .SELECT(decoder_1_out1), .READ_WRITE(READ_WRITE), .CLOCK(CLOCK));
  BC bc_3 (.INPUT(INPUT[0]), .OUTPUT(bc_3_output), .SELECT(decoder_1_out2), .READ_WRITE(READ_WRITE), .CLOCK(CLOCK));
  BC bc_4 (.INPUT(INPUT[0]), .OUTPUT(bc_4_output), .SELECT(decoder_1_out3), .READ_WRITE(READ_WRITE), .CLOCK(CLOCK));
  or or_1 (OUTPUT[0], bc_4_output, bc_3_output, bc_2_output, bc_1_output);
  BC bc_5 (.INPUT(INPUT[1]), .OUTPUT(bc_5_output), .SELECT(decoder_1_out0), .READ_WRITE(READ_WRITE), .CLOCK(CLOCK));
  BC bc_6 (.INPUT(INPUT[1]), .OUTPUT(bc_6_output), .SELECT(decoder_1_out1), .READ_WRITE(READ_WRITE), .CLOCK(CLOCK));
  BC bc_7 (.INPUT(INPUT[1]), .OUTPUT(bc_7_output), .SELECT(decoder_1_out2), .READ_WRITE(READ_WRITE), .CLOCK(CLOCK));
  BC bc_8 (.INPUT(INPUT[1]), .OUTPUT(bc_8_output), .SELECT(decoder_1_out3), .READ_WRITE(READ_WRITE), .CLOCK(CLOCK));
  or or_2 (OUTPUT[1], bc_8_output, bc_7_output, bc_6_output, bc_5_output);
  BC bc_9 (.INPUT(INPUT[2]), .OUTPUT(bc_9_output), .SELECT(decoder_1_out0), .READ_WRITE(READ_WRITE), .CLOCK(CLOCK));
  BC bc_10 (.INPUT(INPUT[2]), .OUTPUT(bc_10_output), .SELECT(decoder_1_out1), .READ_WRITE(READ_WRITE), .CLOCK(CLOCK));
  BC bc_11 (.INPUT(INPUT[2]), .OUTPUT(bc_11_output), .SELECT(decoder_1_out2), .READ_WRITE(READ_WRITE), .CLOCK(CLOCK));
  BC bc_12 (.INPUT(INPUT[2]), .OUTPUT(bc_12_output), .SELECT(decoder_1_out3), .READ_WRITE(READ_WRITE), .CLOCK(CLOCK));
  or or_3 (OUTPUT[2], bc_12_output, bc_11_output, bc_10_output, bc_9_output);
endmodule

module _4x4_BC (
  input  [3:0] INPUT,
  input  ENABLE,
  input  [1:0] ADDRESS,
  input  READ_WRITE,
  input  CLOCK,
  output [3:0] OUTPUT
);

  wire bc_1_output, bc_2_output, bc_3_output, bc_4_output, bc_5_output, bc_6_output, bc_7_output,
       bc_8_output, bc_9_output, bc_10_output, bc_11_output, bc_12_output, bc_13_output, bc_14_output,
       bc_15_output, bc_16_output, decoder_1_out0, decoder_1_out1, decoder_1_out2, decoder_1_out3;

  Decoder #(.select(2)) decoder_1 (
    .out0(decoder_1_out0), .out1(decoder_1_out1), .out2(decoder_1_out2), .out3(decoder_1_out3),
    .sel(ADDRESS), .en(ENABLE));
  BC bc_1 (.INPUT(INPUT[0]), .OUTPUT(bc_1_output), .SELECT(decoder_1_out0), .READ_WRITE(READ_WRITE), .CLOCK(CLOCK));
  BC bc_2 (.INPUT(INPUT[0]), .OUTPUT(bc_2_output), .SELECT(decoder_1_out1), .READ_WRITE(READ_WRITE), .CLOCK(CLOCK));
  BC bc_3 (.INPUT(INPUT[0]), .OUTPUT(bc_3_output), .SELECT(decoder_1_out2), .READ_WRITE(READ_WRITE), .CLOCK(CLOCK));
  BC bc_4 (.INPUT(INPUT[0]), .OUTPUT(bc_4_output), .SELECT(decoder_1_out3), .READ_WRITE(READ_WRITE), .CLOCK(CLOCK));
  or or_1 (OUTPUT[0], bc_4_output, bc_3_output, bc_2_output, bc_1_output);
  BC bc_5 (.INPUT(INPUT[1]), .OUTPUT(bc_5_output), .SELECT(decoder_1_out0), .READ_WRITE(READ_WRITE), .CLOCK(CLOCK));
  BC bc_6 (.INPUT(INPUT[1]), .OUTPUT(bc_6_output), .SELECT(decoder_1_out1), .READ_WRITE(READ_WRITE), .CLOCK(CLOCK));
  BC bc_7 (.INPUT(INPUT[1]), .OUTPUT(bc_7_output), .SELECT(decoder_1_out2), .READ_WRITE(READ_WRITE), .CLOCK(CLOCK));
  BC bc_8 (.INPUT(INPUT[1]), .OUTPUT(bc_8_output), .SELECT(decoder_1_out3), .READ_WRITE(READ_WRITE), .CLOCK(CLOCK));
  or or_2 (OUTPUT[1], bc_8_output, bc_7_output, bc_6_output, bc_5_output);
  BC bc_9 (.INPUT(INPUT[2]), .OUTPUT(bc_9_output), .SELECT(decoder_1_out0), .READ_WRITE(READ_WRITE), .CLOCK(CLOCK));
  BC bc_10 (.INPUT(INPUT[2]), .OUTPUT(bc_10_output), .SELECT(decoder_1_out1), .READ_WRITE(READ_WRITE), .CLOCK(CLOCK));
  BC bc_11 (.INPUT(INPUT[2]), .OUTPUT(bc_11_output), .SELECT(decoder_1_out2), .READ_WRITE(READ_WRITE), .CLOCK(CLOCK));
  BC bc_12 (.INPUT(INPUT[2]), .OUTPUT(bc_12_output), .SELECT(decoder_1_out3), .READ_WRITE(READ_WRITE), .CLOCK(CLOCK));
  or or_3 (OUTPUT[2], bc_12_output, bc_11_output, bc_10_output, bc_9_output);
  BC bc_13 (.INPUT(INPUT[3]), .OUTPUT(bc_13_output), .SELECT(decoder_1_out0), .READ_WRITE(READ_WRITE), .CLOCK(CLOCK));
  BC bc_14 (.INPUT(INPUT[3]), .OUTPUT(bc_14_output), .SELECT(decoder_1_out1), .READ_WRITE(READ_WRITE), .CLOCK(CLOCK));
  BC bc_15 (.INPUT(INPUT[3]), .OUTPUT(bc_15_output), .SELECT(decoder_1_out2), .READ_WRITE(READ_WRITE), .CLOCK(CLOCK));
  BC bc_16 (.INPUT(INPUT[3]), .OUTPUT(bc_16_output), .SELECT(decoder_1_out3), .READ_WRITE(READ_WRITE), .CLOCK(CLOCK));
  or or_4 (OUTPUT[3], bc_16_output, bc_15_output, bc_14_output, bc_13_output);
endmodule
