// Logisim project lab4.circ as structural Verilog: 9 circuits, main circuit main
module main (
  input  [1:0] OP_select,
  input  [1:0] R_address1,
  input  [15:0] W_data,
  input  in_4,
  input  [1:0] R_address2,
  input  [1:0] W_address,
  input  W_en,
  output [15:0] R_data1,
  output [15:0] RESULT,
  output [15:0] R_data2
);

  wire CLOCK_out;
  wire [15:0] multiplexer_1_out;

  Clock CLOCK (.out(CLOCK_out));
  Multiplexer #(.width(16)) multiplexer_1 (
    .in0(W_data), .in1(RESULT), .out(multiplexer_1_out), .sel(in_4));  // open: en
  _16_bit_register_file u_16_bit_register_file_1 (
    .W_data(multiplexer_1_out), .W_address(W_address), .W_en(W_en), .CLOCK(CLOCK_out), .R_data1(R_data1),
    .R_data2(R_data2), .R_en1(1'b1), .R_address2(R_address1), .R_en2(1'b1), .R_address1(R_address2));
  _16_bit_ALU u_16_bit_alu_1 (.A(R_data1), .B(R_data2), .Select(OP_select), .Output(RESULT));  // open: Sum, Cout

  // Notes on the sheet:
  //   0. write manualy
  //   1. store result from ALU
  //   00. AND
  //   01. OR
  //   10. XOR
  //   11. ADD
endmodule

module ALU (
  input  A,
  input  Cin,
  input  B,
  input  [1:0] Select,
  output Output,
  output Cout,
  output Sum
);

  wire and_1_out, or_1_out, xor_1_out;

  and and_1 (and_1_out, A, B);
  or or_1 (or_1_out, A, B);
  xor xor_1 (xor_1_out, A, B);
  Adder adder_1 (.Cin(Cin), .A(A), .B(B), .Cout(Cout), .Sum(Sum));
  Multiplexer #(.select(2)) multiplexer_1 (
    .in0(and_1_out), .in1(or_1_out), .in2(xor_1_out), .in3(Sum), .out(Output), .sel(Select));  // open: en
endmodule

module _4_bit_ALU (
  input  [1:0] Select,
  input  [3:0] in_2,
  input  [3:0] in_3,
  output [3:0] out_4,
  output [3:0] out_5,
  output Cout
);

  wire alu_1_cout, alu_2_cout, alu_3_cout;

  ALU alu_1 (
    .A(in_2[0]), .B(in_3[0]), .Output(out_4[0]), .Cin(1'b0), .Cout(alu_1_cout), .Sum(out_5[0]),
    .Select(Select));
  ALU alu_2 (
    .A(in_2[1]), .B(in_3[1]), .Output(out_4[1]), .Cin(alu_1_cout), .Cout(alu_2_cout), .Sum(out_5[1]),
    .Select(Select));
  ALU alu_3 (
    .A(in_2[2]), .B(in_3[2]), .Output(out_4[2]), .Cin(alu_2_cout), .Cout(alu_3_cout), .Sum(out_5[2]),
    .Select(Select));
  ALU alu_4 (
    .A(in_2[3]), .B(in_3[3]), .Output(out_4[3]), .Cin(alu_3_cout), .Cout(Cout), .Sum(out_5[3]),
    .Select(Select));
endmodule

module _16_bit_ALU (
  input  [1:0] Select,
  input  [15:0] A,
  input  [15:0] B,
  output [15:0] Output,
  output [15:0] Sum,
  output Cout
);

  wire alu_1_cout, alu_2_cout, alu_3_cout, alu_4_cout, alu_5_cout, alu_6_cout, alu_7_cout, alu_8_cout,
       alu_9_cout, alu_10_cout, alu_11_cout, alu_12_cout, alu_13_cout, alu_14_cout, alu_15_cout, and_1_out;
  wire [15:0] alu_1_sum;

  ALU alu_1 (
    .A(A[0]), .B(B[0]), .Output(Output[0]), .Cin(1'b0), .Cout(alu_1_cout), .Sum(alu_1_sum[0]), .Select(Select));
  ALU alu_2 (
    .A(A[1]), .B(B[1]), .Output(Output[1]), .Cin(alu_1_cout), .Cout(alu_2_cout), .Sum(alu_1_sum[1]),
    .Select(Select));
  ALU alu_3 (
    .A(A[2]), .B(B[2]), .Output(Output[2]), .Cin(alu_2_cout), .Cout(alu_3_cout), .Sum(alu_1_sum[2]),
    .Select(Select));
  ALU alu_4 (
    .A(A[3]), .B(B[3]), .Output(Output[3]), .Cin(alu_3_cout), .Cout(alu_4_cout), .Sum(alu_1_sum[3]),
    .Select(Select));
  ALU alu_5 (
    .A(A[4]), .B(B[4]), .Output(Output[4]), .Cin(alu_4_cout), .Cout(alu_5_cout), .Sum(alu_1_sum[4]),
    .Select(Select));
  ALU alu_6 (
    .A(A[5]), .B(B[5]), .Output(Output[5]), .Cin(alu_5_cout), .Cout(alu_6_cout), .Sum(alu_1_sum[5]),
    .Select(Select));
  ALU alu_7 (
    .A(A[6]), .B(B[6]), .Output(Output[6]), .Cin(alu_6_cout), .Cout(alu_7_cout), .Sum(alu_1_sum[6]),
    .Select(Select));
  ALU alu_8 (
    .A(A[7]), .B(B[7]), .Output(Output[7]), .Cin(alu_7_cout), .Cout(alu_8_cout), .Sum(alu_1_sum[7]),
    .Select(Select));
  ALU alu_9 (
    .A(A[8]), .B(B[8]), .Output(Output[8]), .Cin(alu_8_cout), .Cout(alu_9_cout), .Sum(alu_1_sum[8]),
    .Select(Select));
  ALU alu_10 (
    .A(A[9]), .B(B[9]), .Output(Output[9]), .Cin(alu_9_cout), .Cout(alu_10_cout), .Sum(alu_1_sum[9]),
    .Select(Select));
  ALU alu_11 (
    .A(A[10]), .B(B[10]), .Output(Output[10]), .Cin(alu_10_cout), .Cout(alu_11_cout), .Sum(alu_1_sum[10]),
    .Select(Select));
  ALU alu_12 (
    .A(A[11]), .B(B[11]), .Output(Output[11]), .Cin(alu_11_cout), .Cout(alu_12_cout), .Sum(alu_1_sum[11]),
    .Select(Select));
  ALU alu_13 (
    .A(A[12]), .B(B[12]), .Output(Output[12]), .Cin(alu_12_cout), .Cout(alu_13_cout), .Sum(alu_1_sum[12]),
    .Select(Select));
  ALU alu_14 (
    .A(A[13]), .B(B[13]), .Output(Output[13]), .Cin(alu_13_cout), .Cout(alu_14_cout), .Sum(alu_1_sum[13]),
    .Select(Select));
  ALU alu_15 (
    .A(A[14]), .B(B[14]), .Output(Output[14]), .Cin(alu_14_cout), .Cout(alu_15_cout), .Sum(alu_1_sum[14]),
    .Select(Select));
  ALU alu_16 (
    .A(A[15]), .B(B[15]), .Output(Output[15]), .Cin(alu_15_cout), .Cout(Cout), .Sum(alu_1_sum[15]),
    .Select(Select));
  and and_1 (and_1_out, Select[0], Select[1]);
  assign Sum = and_1_out ? alu_1_sum : 16'bz;  // Controlled_Buffer controlled_buffer_1
endmodule

module Another_16_bit (
  input  [1:0] Select,
  input  [15:0] A,
  input  [15:0] B,
  output [15:0] Output,
  output [15:0] Sum,
  output Cout
);

  wire and_1_out, n4_bit_alu_1_cout, n4_bit_alu_2_cout, n4_bit_alu_3_cout;
  wire [15:0] n4_bit_alu_1_out_5;

  _4_bit_ALU u_4_bit_alu_1 (
    .in_2(A[3:0]), .in_3(B[3:0]), .out_4(Output[3:0]), .out_5(n4_bit_alu_1_out_5[3:0]),
    .Cout(n4_bit_alu_1_cout), .Select(Select));
  _4_bit_ALU u_4_bit_alu_2 (
    .in_2(A[7:4]), .in_3(B[7:4]), .out_4(Output[7:4]), .out_5(n4_bit_alu_1_out_5[7:4]),
    .Cout(n4_bit_alu_2_cout), .Select(Select));
  _4_bit_ALU u_4_bit_alu_3 (
    .in_2(A[11:8]), .in_3(B[11:8]), .out_4(Output[11:8]), .out_5(n4_bit_alu_1_out_5[11:8]),
    .Cout(n4_bit_alu_3_cout), .Select(Select));
  _4_bit_ALU u_4_bit_alu_4 (
    .in_2(A[15:12]), .in_3(B[15:12]), .out_4(Output[15:12]), .out_5(n4_bit_alu_1_out_5[15:12]), .Cout(Cout),
    .Select(Select));
  and and_1 (and_1_out, Select[0], Select[1]);
  assign Sum = and_1_out ? n4_bit_alu_1_out_5 : 16'bz;  // Controlled_Buffer controlled_buffer_1
endmodule

module Adder (
  input  Cin,
  input  A,
  input  B,
  output Cout,
  output Sum
);

  wire and_1_out, and_2_out, xor_1_out;

  and and_1 (and_1_out, B, A);
  xor xor_1 (xor_1_out, A, B);
  and and_2 (and_2_out, Cin, xor_1_out);
  or or_1 (Cout, and_2_out, and_1_out);
  xor xor_2 (Sum, Cin, xor_1_out);
endmodule

module _16_bit_register (
  input  [15:0] INPUT,
  input  _0,
  input  ENABLE,
  input  CLOCK,
  output [15:0] OUTPUT
);

  D_Flip_Flop d_ff_1 (.clk(CLOCK), .D(INPUT[0]), .Q(OUTPUT[0]), .en(ENABLE), .reset(_0));  // open: Qn, preset
  D_Flip_Flop d_ff_2 (.clk(CLOCK), .D(INPUT[4]), .Q(OUTPUT[4]), .en(ENABLE), .reset(_0));  // open: Qn, preset
  D_Flip_Flop d_ff_3 (.clk(CLOCK), .D(INPUT[8]), .Q(OUTPUT[8]), .en(ENABLE), .reset(_0));  // open: Qn, preset
  D_Flip_Flop d_ff_4 (.clk(CLOCK), .D(INPUT[12]), .Q(OUTPUT[12]), .en(ENABLE), .reset(_0));  // open: Qn, preset
  D_Flip_Flop d_ff_5 (.clk(CLOCK), .D(INPUT[1]), .Q(OUTPUT[1]), .en(ENABLE), .reset(_0));  // open: Qn, preset
  D_Flip_Flop d_ff_6 (.clk(CLOCK), .D(INPUT[5]), .Q(OUTPUT[5]), .en(ENABLE), .reset(_0));  // open: Qn, preset
  D_Flip_Flop d_ff_7 (.clk(CLOCK), .D(INPUT[9]), .Q(OUTPUT[9]), .en(ENABLE), .reset(_0));  // open: Qn, preset
  D_Flip_Flop d_ff_8 (.clk(CLOCK), .D(INPUT[13]), .Q(OUTPUT[13]), .en(ENABLE), .reset(_0));  // open: Qn, preset
  D_Flip_Flop d_ff_9 (.clk(CLOCK), .D(INPUT[2]), .Q(OUTPUT[2]), .en(ENABLE), .reset(_0));  // open: Qn, preset
  D_Flip_Flop d_ff_10 (.clk(CLOCK), .D(INPUT[6]), .Q(OUTPUT[6]), .en(ENABLE), .reset(_0));  // open: Qn, preset
  D_Flip_Flop d_ff_11 (.clk(CLOCK), .D(INPUT[10]), .Q(OUTPUT[10]), .en(ENABLE), .reset(_0));  // open: Qn, preset
  D_Flip_Flop d_ff_12 (.clk(CLOCK), .D(INPUT[14]), .Q(OUTPUT[14]), .en(ENABLE), .reset(_0));  // open: Qn, preset
  D_Flip_Flop d_ff_13 (.clk(CLOCK), .D(INPUT[3]), .Q(OUTPUT[3]), .en(ENABLE), .reset(_0));  // open: Qn, preset
  D_Flip_Flop d_ff_14 (.clk(CLOCK), .D(INPUT[7]), .Q(OUTPUT[7]), .en(ENABLE), .reset(_0));  // open: Qn, preset
  D_Flip_Flop d_ff_15 (.clk(CLOCK), .D(INPUT[11]), .Q(OUTPUT[11]), .en(ENABLE), .reset(_0));  // open: Qn, preset
  D_Flip_Flop d_ff_16 (.clk(CLOCK), .D(INPUT[15]), .Q(OUTPUT[15]), .en(ENABLE), .reset(_0));  // open: Qn, preset
endmodule

module _16_bit_register_file (
  input  R_en1,
  input  [1:0] R_address2,
  input  [15:0] W_data,
  input  [1:0] W_address,
  input  W_en,
  input  CLOCK,
  input  R_en2,
  input  [1:0] R_address1,
  output [15:0] R_data1,
  output [15:0] R_data2
);

  wire decoder_1_out0, decoder_1_out1, decoder_1_out2, decoder_1_out3;
  wire [15:0] n16_bit_register_1_output, n16_bit_register_2_output, n16_bit_register_3_output,
       n16_bit_register_4_output;

  Decoder #(.select(2), .disabled(0)) decoder_1 (
    .out0(decoder_1_out0), .out1(decoder_1_out1), .out2(decoder_1_out2), .out3(decoder_1_out3),
    .sel(W_address), .en(W_en));
  _16_bit_register u_16_bit_register_1 (
    .INPUT(W_data), .ENABLE(decoder_1_out0), .CLOCK(CLOCK), .OUTPUT(n16_bit_register_1_output));  // open: _0
  _16_bit_register u_16_bit_register_2 (
    .INPUT(W_data), .ENABLE(decoder_1_out1), .CLOCK(CLOCK), .OUTPUT(n16_bit_register_2_output));  // open: _0
  _16_bit_register u_16_bit_register_3 (
    .INPUT(W_data), .ENABLE(decoder_1_out2), .CLOCK(CLOCK), .OUTPUT(n16_bit_register_3_output));  // open: _0
  _16_bit_register u_16_bit_register_4 (
    .INPUT(W_data), .ENABLE(decoder_1_out3), .CLOCK(CLOCK), .OUTPUT(n16_bit_register_4_output));  // open: _0
  Multiplexer #(.select(2), .width(16)) multiplexer_1 (
    .in0(n16_bit_register_1_output), .in1(n16_bit_register_2_output), .in2(n16_bit_register_3_output),
    .in3(n16_bit_register_4_output), .out(R_data1), .sel(R_address2), .en(R_en1));
  Multiplexer #(.select(2), .width(16)) multiplexer_2 (
    .in0(n16_bit_register_1_output), .in1(n16_bit_register_2_output), .in2(n16_bit_register_3_output),
    .in3(n16_bit_register_4_output), .out(R_data2), .sel(R_address1), .en(R_en2));
endmodule

module register_file_test (
  input  R_en1,
  input  [1:0] R_address1,
  input  [15:0] W_data,
  input  [1:0] W_address,
  input  R_en2,
  input  [1:0] R_address2,
  input  W_en,
  output [15:0] R_data1,
  output [15:0] R_data2
);

  wire CLOCK_out;

  Clock CLOCK (.out(CLOCK_out));
  _16_bit_register_file u_16_bit_register_file_1 (
    .W_data(W_data), .W_address(W_address), .W_en(W_en), .CLOCK(CLOCK_out), .R_data1(R_data1),
    .R_data2(R_data2), .R_en1(R_en1), .R_address2(R_address1), .R_en2(R_en2), .R_address1(R_address2));
endmodule
