// Logisim project lab6.circ as structural Verilog: 5 circuits, main circuit main
module main (
  input  [31:0] in_1,
  input  [31:0] in_2,
  input  [5:0] funct,
  input  [5:0] op_code,
  output out_5,
  output [31:0] out_6,
  output [3:0] out_7
);

  wire [2:0] cu_1_aluop_2_1_0;

  CU cu_1 (
    .OP_CODE(op_code), .ALUOp_2_1_0(cu_1_aluop_2_1_0));  // open: RegDst, ALUSrc, MemtoReg, RegWrite, MemRead, MemWrite, Branch, Jump
  ALU_Control alu_control_1 (.funct(funct), .ALUOp(cu_1_aluop_2_1_0), .ALU_Cinput(out_7));
  _32_bit_ALU u_32_bit_alu_1 (.ALU_Cinput(out_7), .A(in_1), .B(in_2), .zero(out_5), .result(out_6));

  // Notes on the sheet:
  //   Umar S Salah 120182428
  //   Mohammad H Mansour 120180606
endmodule

module CU (
  input  [5:0] OP_CODE,
  output RegDst,
  output ALUSrc,
  output MemtoReg,
  output RegWrite,
  output MemRead,
  output MemWrite,
  output Branch,
  output [2:0] ALUOp_2_1_0,
  output Jump
);

  wire addi_out, andi_out, ori_out, slti_out, xori_out;

  and slti (slti_out, ~OP_CODE[5], ~OP_CODE[4], OP_CODE[3], ~OP_CODE[2], OP_CODE[1], ~OP_CODE[0]);  // AND_Gate
  and xori (xori_out, ~OP_CODE[5], ~OP_CODE[4], OP_CODE[3], OP_CODE[2], OP_CODE[1], ~OP_CODE[0]);  // AND_Gate
  and andi (andi_out, ~OP_CODE[5], ~OP_CODE[4], OP_CODE[3], OP_CODE[2], ~OP_CODE[1], ~OP_CODE[0]);  // AND_Gate
  and ori (ori_out, ~OP_CODE[5], ~OP_CODE[4], OP_CODE[3], OP_CODE[2], ~OP_CODE[1], OP_CODE[0]);  // AND_Gate
  and addi (addi_out, ~OP_CODE[5], ~OP_CODE[4], OP_CODE[3], ~OP_CODE[2], ~OP_CODE[1], ~OP_CODE[0]);  // AND_Gate
  and j (Jump, ~OP_CODE[5], ~OP_CODE[4], ~OP_CODE[3], ~OP_CODE[2], OP_CODE[1], ~OP_CODE[0]);  // AND_Gate
  and beq (Branch, ~OP_CODE[5], ~OP_CODE[4], ~OP_CODE[3], OP_CODE[2], ~OP_CODE[1], ~OP_CODE[0]);  // AND_Gate
  and sw (MemWrite, OP_CODE[5], ~OP_CODE[4], OP_CODE[3], ~OP_CODE[2], OP_CODE[1], OP_CODE[0]);  // AND_Gate
  and lw (MemRead, OP_CODE[5], ~OP_CODE[4], ~OP_CODE[3], ~OP_CODE[2], OP_CODE[1], OP_CODE[0]);  // AND_Gate
  or or_1 (ALUOp_2_1_0[0], Branch, addi_out, xori_out, andi_out);
  or or_2 (ALUOp_2_1_0[1], ori_out, andi_out, addi_out, slti_out);
  or or_3 (ALUOp_2_1_0[2], RegDst, xori_out, slti_out, addi_out);
  and r_type (RegDst, ~OP_CODE[5], ~OP_CODE[4], ~OP_CODE[3], ~OP_CODE[2], ~OP_CODE[1], ~OP_CODE[0]);  // AND_Gate
  or or_4 (ALUSrc, slti_out, ori_out, MemRead, addi_out, MemWrite, andi_out, xori_out);
  or or_5 (RegWrite, xori_out, ori_out, RegDst, addi_out, MemRead, andi_out, slti_out);

  assign MemtoReg = MemRead;

  // Notes on the sheet:
  //   000          lw / sw
  //   001          beq
  //   010          ori        
  //   011          andi     
  //   100           r-type 
  //   101           xori
  //   110           slti
  //   111           addi
endmodule

module ALU_Control (
  input  [5:0] funct,
  input  [2:0] ALUOp,
  output [3:0] ALU_Cinput
);

  wire add_out, addi_out, beq_out, lw_out, nor_out, or_4_out, ori_out, slt_out, slti_out, sub_out, sw_out,
       xor_out, xori_out;

  and \nor  (nor_out, ALUOp[2], ~ALUOp[1], ~ALUOp[0], funct[5], ~funct[4], ~funct[3], funct[2], funct[1], funct[0]);  // AND_Gate
  and xori (xori_out, ALUOp[2], ~ALUOp[1], ALUOp[0]);  // AND_Gate
  and slti (slti_out, ALUOp[2], ALUOp[1], ~ALUOp[0]);  // AND_Gate
  and addi (addi_out, ALUOp[2], ALUOp[1], ALUOp[0]);
  // AND_Gate andi has open pins: in0=ALUOp[2], in1=ALUOp[1], in2=ALUOp[0], out=open
  and ori (ori_out, ~ALUOp[2], ALUOp[1], ~ALUOp[0]);  // AND_Gate
  and beq (beq_out, ~ALUOp[2], ~ALUOp[1], ALUOp[0]);  // AND_Gate
  and sw (sw_out, ~ALUOp[2], ~ALUOp[1], ~ALUOp[0]);  // AND_Gate
  or or_1 (ALU_Cinput[3], slt_out, beq_out, sub_out, slti_out);
  and lw (lw_out, ~ALUOp[2], ~ALUOp[1], ~ALUOp[0]);  // AND_Gate
  or or_2 (ALU_Cinput[2], xori_out, nor_out, xor_out);
  or or_3 (ALU_Cinput[1], addi_out, slt_out, slti_out, beq_out, sub_out, sw_out, lw_out, add_out);
  and slt (slt_out, ALUOp[2], ~ALUOp[1], ~ALUOp[0], funct[5], ~funct[4], funct[3], ~funct[2], funct[1], ~funct[0]);  // AND_Gate
  and \xor  (xor_out, ALUOp[2], ~ALUOp[1], ~ALUOp[0], funct[5], ~funct[4], ~funct[3], funct[2], funct[1], ~funct[0]);  // AND_Gate
  and or_4 (or_4_out, ALUOp[2], ~ALUOp[1], ~ALUOp[0], funct[5], ~funct[4], ~funct[3], funct[2], ~funct[1], funct[0]);  // AND_Gate
  // AND_Gate and has open pins: in0=ALUOp[2], in1=ALUOp[1], in2=ALUOp[0], in3=funct[5], in4=funct[4], in5=funct[3], in6=funct[2], in7=funct[1], in8=funct[0], out=open
  or or_5 (ALU_Cinput[0], slti_out, slt_out, nor_out, ori_out, or_4_out);
  and sub (sub_out, ALUOp[2], ~ALUOp[1], ~ALUOp[0], funct[5], ~funct[4], ~funct[3], ~funct[2], funct[1], ~funct[0]);  // AND_Gate
  and add (add_out, ALUOp[2], ~ALUOp[1], ~ALUOp[0], funct[5], ~funct[4], ~funct[3], ~funct[2], ~funct[1], ~funct[0]);  // AND_Gate

  // Notes on the sheet:
  //   0010   add
  //   1010   sub
  //   0000   and
  //   0001   or
  //   0100   xor
  //   1011   slt
  //   1010   beq
  //   0001   ori
  //   0000   andi
  //   0010   addi
  //   1011   slti
  //   0100   xori
  //   0010   lw / sw
endmodule

module ALU (
  input  c_in,
  input  A,
  input  B,
  input  [3:0] ALU_Cinput,
  output ZERO,
  output \output ,
  output c_out
);

  wire adder_1_out, and_1_out, multiplexer_1_out, not_1_out, not_2_out, not_3_out, or_1_out, xor_1_out;

  not not_1 (not_1_out, B);
  Multiplexer multiplexer_1 (.in0(B), .in1(not_1_out), .out(multiplexer_1_out), .sel(ALU_Cinput[3]));  // open: en
  and and_1 (and_1_out, A, multiplexer_1_out);
  or or_1 (or_1_out, A, multiplexer_1_out);
  Adder #(.width(1)) adder_1 (.a(A), .b(multiplexer_1_out), .out(adder_1_out), .cin(c_in), .cout(c_out));
  xor xor_1 (xor_1_out, A, multiplexer_1_out);
  not not_2 (not_2_out, c_out);
  not not_3 (not_3_out, or_1_out);
  not not_4 (ZERO, \output );
  Multiplexer #(.select(3)) multiplexer_2 (
    .in0(and_1_out), .in1(or_1_out), .in2(adder_1_out), .in3(not_2_out), .in4(xor_1_out), .in5(not_3_out),
    .in6(1'b0), .in7(1'b0), .out(\output ), .sel(ALU_Cinput[2:0]));  // open: en
endmodule

module _32_bit_ALU (
  input  [3:0] ALU_Cinput,
  input  [31:0] A,
  input  [31:0] B,
  output zero,
  output [31:0] result
);

  wire alu_1_c_out, alu_1_zero, alu_2_c_out, alu_2_zero, alu_3_c_out, alu_3_zero, alu_4_c_out, alu_4_zero,
       alu_5_c_out, alu_5_zero, alu_6_c_out, alu_6_zero, alu_7_c_out, alu_7_zero, alu_8_c_out, alu_8_zero,
       alu_9_c_out, alu_9_zero, alu_10_c_out, alu_10_zero, alu_11_c_out, alu_11_zero, alu_12_c_out,
       alu_12_zero, alu_13_c_out, alu_13_zero, alu_14_c_out, alu_14_zero, alu_15_c_out, alu_15_zero,
       alu_16_c_out, alu_16_zero, alu_17_c_out, alu_17_zero, alu_18_c_out, alu_18_zero, alu_19_c_out,
       alu_19_zero, alu_20_c_out, alu_20_zero, alu_21_c_out, alu_21_zero, alu_22_c_out, alu_22_zero,
       alu_23_c_out, alu_23_zero, alu_24_c_out, alu_24_zero, alu_25_c_out, alu_25_zero, alu_26_c_out,
       alu_26_zero, alu_27_c_out, alu_27_zero, alu_28_c_out, alu_28_zero, alu_29_c_out, alu_29_zero,
       alu_30_c_out, alu_30_zero, alu_31_c_out, alu_31_zero, alu_32_c_out, alu_32_zero, and_1_out;
  wire [31:0] alu_1_output;

  ALU alu_1 (
    .A(A[0]), .B(B[0]), .ZERO(alu_1_zero), .\output (alu_1_output[0]), .c_out(alu_1_c_out),
    .c_in(ALU_Cinput[3]), .ALU_Cinput(ALU_Cinput));
  ALU alu_2 (
    .A(A[1]), .B(B[1]), .ZERO(alu_2_zero), .\output (alu_1_output[1]), .c_out(alu_2_c_out),
    .c_in(alu_1_c_out), .ALU_Cinput(ALU_Cinput));
  ALU alu_3 (
    .A(A[2]), .B(B[2]), .ZERO(alu_3_zero), .\output (alu_1_output[2]), .c_out(alu_3_c_out),
    .c_in(alu_2_c_out), .ALU_Cinput(ALU_Cinput));
  ALU alu_4 (
    .A(A[3]), .B(B[3]), .ZERO(alu_4_zero), .\output (alu_1_output[3]), .c_out(alu_4_c_out),
    .c_in(alu_3_c_out), .ALU_Cinput(ALU_Cinput));
  ALU alu_5 (
    .A(A[4]), .B(B[4]), .ZERO(alu_5_zero), .\output (alu_1_output[4]), .c_out(alu_5_c_out),
    .c_in(alu_4_c_out), .ALU_Cinput(ALU_Cinput));
  ALU alu_6 (
    .A(A[5]), .B(B[5]), .ZERO(alu_6_zero), .\output (alu_1_output[5]), .c_out(alu_6_c_out),
    .c_in(alu_5_c_out), .ALU_Cinput(ALU_Cinput));
  ALU alu_7 (
    .A(A[6]), .B(B[6]), .ZERO(alu_7_zero), .\output (alu_1_output[6]), .c_out(alu_7_c_out),
    .c_in(alu_6_c_out), .ALU_Cinput(ALU_Cinput));
  ALU alu_8 (
    .A(A[7]), .B(B[7]), .ZERO(alu_8_zero), .\output (alu_1_output[7]), .c_out(alu_8_c_out),
    .c_in(alu_7_c_out), .ALU_Cinput(ALU_Cinput));
  ALU alu_9 (
    .A(A[8]), .B(B[8]), .ZERO(alu_9_zero), .\output (alu_1_output[8]), .c_out(alu_9_c_out),
    .c_in(alu_8_c_out), .ALU_Cinput(ALU_Cinput));
  ALU alu_10 (
    .A(A[9]), .B(B[9]), .ZERO(alu_10_zero), .\output (alu_1_output[9]), .c_out(alu_10_c_out),
    .c_in(alu_9_c_out), .ALU_Cinput(ALU_Cinput));
  ALU alu_11 (
    .A(A[10]), .B(B[10]), .ZERO(alu_11_zero), .\output (alu_1_output[10]), .c_out(alu_11_c_out),
    .c_in(alu_10_c_out), .ALU_Cinput(ALU_Cinput));
  ALU alu_12 (
    .A(A[11]), .B(B[11]), .ZERO(alu_12_zero), .\output (alu_1_output[11]), .c_out(alu_12_c_out),
    .c_in(alu_11_c_out), .ALU_Cinput(ALU_Cinput));
  ALU alu_13 (
    .A(A[12]), .B(B[12]), .ZERO(alu_13_zero), .\output (alu_1_output[12]), .c_out(alu_13_c_out),
    .c_in(alu_12_c_out), .ALU_Cinput(ALU_Cinput));
  ALU alu_14 (
    .A(A[13]), .B(B[13]), .ZERO(alu_14_zero), .\output (alu_1_output[13]), .c_out(alu_14_c_out),
    .c_in(alu_13_c_out), .ALU_Cinput(ALU_Cinput));
  ALU alu_15 (
    .A(A[14]), .B(B[14]), .ZERO(alu_15_zero), .\output (alu_1_output[14]), .c_out(alu_15_c_out),
    .c_in(alu_14_c_out), .ALU_Cinput(ALU_Cinput));
  ALU alu_16 (
    .A(A[15]), .B(B[15]), .ZERO(alu_16_zero), .\output (alu_1_output[15]), .c_out(alu_16_c_out),
    .c_in(alu_15_c_out), .ALU_Cinput(ALU_Cinput));
  ALU alu_17 (
    .A(A[16]), .B(B[16]), .ZERO(alu_17_zero), .\output (alu_1_output[16]), .c_out(alu_17_c_out),
    .c_in(alu_16_c_out), .ALU_Cinput(ALU_Cinput));
  ALU alu_18 (
    .A(A[17]), .B(B[17]), .ZERO(alu_18_zero), .\output (alu_1_output[17]), .c_out(alu_18_c_out),
    .c_in(alu_17_c_out), .ALU_Cinput(ALU_Cinput));
  ALU alu_19 (
    .A(A[18]), .B(B[18]), .ZERO(alu_19_zero), .\output (alu_1_output[18]), .c_out(alu_19_c_out),
    .c_in(alu_18_c_out), .ALU_Cinput(ALU_Cinput));
  ALU alu_20 (
    .A(A[19]), .B(B[19]), .ZERO(alu_20_zero), .\output (alu_1_output[19]), .c_out(alu_20_c_out),
    .c_in(alu_19_c_out), .ALU_Cinput(ALU_Cinput));
  ALU alu_21 (
    .A(A[20]), .B(B[20]), .ZERO(alu_21_zero), .\output (alu_1_output[20]), .c_out(alu_21_c_out),
    .c_in(alu_20_c_out), .ALU_Cinput(ALU_Cinput));
  ALU alu_22 (
    .A(A[21]), .B(B[21]), .ZERO(alu_22_zero), .\output (alu_1_output[21]), .c_out(alu_22_c_out),
    .c_in(alu_21_c_out), .ALU_Cinput(ALU_Cinput));
  ALU alu_23 (
    .A(A[22]), .B(B[22]), .ZERO(alu_23_zero), .\output (alu_1_output[22]), .c_out(alu_23_c_out),
    .c_in(alu_22_c_out), .ALU_Cinput(ALU_Cinput));
  ALU alu_24 (
    .A(A[23]), .B(B[23]), .ZERO(alu_24_zero), .\output (alu_1_output[23]), .c_out(alu_24_c_out),
    .c_in(alu_23_c_out), .ALU_Cinput(ALU_Cinput));
  ALU alu_25 (
    .A(A[24]), .B(B[24]), .ZERO(alu_25_zero), .\output (alu_1_output[24]), .c_out(alu_25_c_out),
    .c_in(alu_24_c_out), .ALU_Cinput(ALU_Cinput));
  ALU alu_26 (
    .A(A[25]), .B(B[25]), .ZERO(alu_26_zero), .\output (alu_1_output[25]), .c_out(alu_26_c_out),
    .c_in(alu_25_c_out), .ALU_Cinput(ALU_Cinput));
  ALU alu_27 (
    .A(A[26]), .B(B[26]), .ZERO(alu_27_zero), .\output (alu_1_output[26]), .c_out(alu_27_c_out),
    .c_in(alu_26_c_out), .ALU_Cinput(ALU_Cinput));
  ALU alu_28 (
    .A(A[27]), .B(B[27]), .ZERO(alu_28_zero), .\output (alu_1_output[27]), .c_out(alu_28_c_out),
    .c_in(alu_27_c_out), .ALU_Cinput(ALU_Cinput));
  ALU alu_29 (
    .A(A[28]), .B(B[28]), .ZERO(alu_29_zero), .\output (alu_1_output[28]), .c_out(alu_29_c_out),
    .c_in(alu_28_c_out), .ALU_Cinput(ALU_Cinput));
  ALU alu_30 (
    .A(A[29]), .B(B[29]), .ZERO(alu_30_zero), .\output (alu_1_output[29]), .c_out(alu_30_c_out),
    .c_in(alu_29_c_out), .ALU_Cinput(ALU_Cinput));
  ALU alu_31 (
    .A(A[30]), .B(B[30]), .ZERO(alu_31_zero), .\output (alu_1_output[30]), .c_out(alu_31_c_out),
    .c_in(alu_30_c_out), .ALU_Cinput(ALU_Cinput));
  ALU alu_32 (
    .A(A[31]), .B(B[31]), .ZERO(alu_32_zero), .\output (alu_1_output[31]), .c_out(alu_32_c_out),
    .c_in(alu_31_c_out), .ALU_Cinput(ALU_Cinput));
  and and_1 (and_1_out, ALU_Cinput[0], ALU_Cinput[1], ~ALU_Cinput[2], ALU_Cinput[3], ~alu_32_c_out);  // AND_Gate
  Multiplexer #(.width(32)) multiplexer_1 (.in0(alu_1_output), .in1(32'h1), .out(result), .sel(and_1_out));  // open: en
  and and_2 (zero, alu_1_zero, alu_2_zero, alu_3_zero, alu_4_zero, alu_5_zero, alu_6_zero, alu_7_zero, alu_8_zero, alu_9_zero, alu_10_zero, alu_11_zero, alu_12_zero, alu_13_zero, alu_14_zero, alu_15_zero, alu_16_zero, alu_17_zero, alu_18_zero, alu_19_zero, alu_20_zero, alu_21_zero, alu_22_zero, alu_23_zero, alu_24_zero, alu_25_zero, alu_26_zero, alu_27_zero, alu_28_zero, alu_29_zero, alu_30_zero, alu_31_zero, alu_32_zero);
endmodule
